# Fritzing sketch Variable current NJM2732 (saved by Fritzing 0.9.3b)
breadboards: 1

parts:
  IC1 = Dual Op-Amp [package=dip08]
  Q1 = NPN-Transistor [package="TO92 [THT]"]
  Q2 = NPN-Transistor [package="TO92 [THT]"]
  R1 = Resistor [tolerance=±5% resistance=1k package=THT]
  R2 = Resistor [tolerance=±5% resistance=1k package=THT]
  Q3 = PNP-Transistor [package="TO92 [THT]"]
  Q4 = PNP-Transistor [package="TO92 [THT]"]
  R3 = Resistor [tolerance=±5% resistance=220 package=THT]
  R4 = Resistor [tolerance=±5% resistance=1k package=THT]
  R5 = Rotary Potentiometer (Small) [maximum_resistance=100kΩ package=THT]
  C1 = Electrolytic Capacitor [capacitance=1µF package="100 mil [THT, electrolytic]"]

nets:
  N1: IC1.A_OUT, Q1.C
  N2: IC1.A_-IN, Q2.E, R1.Pin_0
  N3: IC1.A_+IN, R5.wiper
  N4: IC1.A_V-, R1.Pin_1, R3.Pin_0, R5.leg2, C1.-
  N5: IC1.B_+IN, Q1.B, Q2.B, R2.Pin_1
  N6: IC1.B_-IN, Q4.E, R4.Pin_1
  N7: IC1.B_OUT, Q3.C
  N8: IC1.A_V+, R2.Pin_0, R4.Pin_0, R5.leg1, C1.+
  N9: Q1.E, Q2.C
  N10: Q3.E, Q4.C
  N11: Q3.B, Q4.B, R3.Pin_1

notes:
  RL
  GND
  +5V
  GND
  INPUT
  +5V
